# Fritzing sketch turntable (saved by Fritzing 0.9.1b)
breadboards: 1

parts:
  M1 = DC Motor
  D1 = Zener Diode [part_number=1N4732A breakdown_voltage=3.6V package="300 mil [THT]"]  # not connected
  R1 = Resistor [tolerance=±5% resistance=1k package=THT]
  Q1 = NPN-Transistor [package="SOT-23 [SMD]"]
  Part1 = Arduino Leonardo (Rev3b)
  J6 = Power Jack [package=power_jack_smd]
  R2 = Rotary Potentiometer (Small) [maximum_resistance=10kΩ package=THT]
  R3 = Resistor [tolerance=±5% resistance=100 package=THT]
  R4 = Resistor [tolerance=±5% resistance=160 package=THT]
  R5 = Resistor [tolerance=±5% resistance=220 package=THT]
  R6 = Resistor [tolerance=±5% resistance=330 package=THT]
  R7 = Resistor [tolerance=±5% resistance=680 package=THT]
  R8 = Resistor [tolerance=±5% resistance=470 package=THT]
  R9 = Resistor [tolerance=±5% resistance=1k package=THT]
  S1 = Square Pushbutton
  S2 = Square Pushbutton
  S3 = Square Pushbutton
  S4 = Square Pushbutton
  S5 = Square Pushbutton
  S6 = Square Pushbutton
  R10 = Rotary Potentiometer (Small) [maximum_resistance=10kΩ package=THT]
  Q2 = LTR-301 [package=ltr-301]
  LED2 = smd LED [color="Infrared (850nm)" package="0603 [SMD]"]
  R11 = Resistor [tolerance=±5% resistance=1M package=THT]
  R12 = Resistor [tolerance=±5% resistance=270 package=THT]
  Q4 = PNP-Transistor [package="TO92 [THT]"]
  D2 = Zener Diode [part_number=1N4732A breakdown_voltage=3.6V package="300 mil [THT]"]
  D3 = Zener Diode [part_number=1N4732A breakdown_voltage=3.6V package="300 mil [THT]"]
  D4 = Zener Diode [part_number=1N4732A breakdown_voltage=3.6V package="300 mil [THT]"]
  R13 = Resistor [tolerance=±5% resistance=1k package=THT]
  R15 = Resistor [tolerance=±5% resistance=100 package=THT]
  R17 = Resistor [tolerance=±5% resistance=100 package=THT]
  Q6 = NPN-Transistor [package="SOT-23 [SMD]"]
  Q7 = PNP-Transistor [package="TO92 [THT]"]
  Q8 = PNP-Transistor [package="TO92 [THT]"]  # not connected
  R22 = Rotary Potentiometer (Small) [maximum_resistance=10kΩ package=THT]
  LED3 = LED - 5mm [color="Red (633nm)" package="5 mm [THT]"]
  R23 = Resistor [tolerance=±5% resistance=220 package=THT]
  R26 = Resistor [tolerance=±5% resistance=220 package=THT]
  R27 = Resistor [tolerance=±5% resistance=220 package=THT]
  R25 = Resistor [tolerance=±5% resistance=220 package=THT]
  R24 = Resistor [tolerance=±5% resistance=220 package=THT]
  R28 = Resistor [tolerance=±5% resistance=220 package=THT]
  LED9 = LED - 5mm [color="Red (633nm)" package="5 mm [THT]"]
  LED10 = LED - 5mm [color="Red (633nm)" package="5 mm [THT]"]
  LED11 = LED - 5mm [color="Red (633nm)" package="5 mm [THT]"]
  LED12 = LED - 5mm [color="Red (633nm)" package="5 mm [THT]"]
  LED13 = LED - 5mm [color="Red (633nm)" package="5 mm [THT]"]
  U1 = SWITCH_SPDT [package=kps-1290]

nets:
  N1: M1.pin_1, D4.cathode
  N2: M1.pin_2, D2.anode, D3.cathode
  N3: R1.Pin_0, Q1.0
  GND: Q1.2, Part1.GND, J6.GND, R2.leg1, R2.leg2, R3.Pin_1, R4.Pin_1, R5.Pin_1, R6.Pin_1, R7.Pin_1, R8.Pin_1, R9.Pin_1, R10.leg1, Q2.E, LED2.cathode, Q6.2, R22.leg1, LED3.cathode, LED9.cathode, LED10.cathode, LED11.cathode, LED12.cathode, LED13.cathode, U1.P
  N4: Q1.1, R15.Pin_0
  N5: Part1.D2/SDA, Part1.A1, R9.Pin_0, S1.leg0, S2.leg0, S3.leg0, S4.leg0, S5.leg0, S6.leg0, R10.leg2, R22.leg2
  N6: Part1.D7, U1.S
  N7: Part1.5V, J6.PWR, R11.Pin_0, R12.Pin_0, Q4.E, Q7.E
  N8: Part1.A0, R2.wiper
  N9: Part1.A2, Q2.C, R11.Pin_1
  N10: Part1.A3, R10.wiper
  N11: Part1.A4, R22.wiper
  N12: Part1.D8/A8, R27.Pin_1
  N13: Part1.D9_PWM/A9, R26.Pin_1
  N14: Part1.D10_PWM/A10, R25.Pin_1
  N15: Part1.D11_PWM, R24.Pin_1
  N16: Part1.D12/A11, R28.Pin_1
  N17: Part1.D13_PWM, R23.Pin_1
  N18: R3.Pin_0, S5.leg1
  N19: R4.Pin_0, S6.leg1
  N20: R5.Pin_0, S2.leg1
  N21: R6.Pin_0, S1.leg1
  N22: R7.Pin_0, S3.leg1
  N23: R8.Pin_0, S4.leg1
  N24: LED2.anode, R12.Pin_1
  N25: Q4.B, R15.Pin_1
  N26: Q4.C, D3.anode
  N27: D2.cathode, R17.Pin_0, Q6.1
  N28: D4.anode, Q7.C
  N29: R13.Pin_0, Q6.0
  N30: R17.Pin_1, Q7.B
  N31: LED3.anode, R23.Pin_0
  N32: R26.Pin_0, LED12.anode
  N33: R27.Pin_0, LED13.anode
  N34: R25.Pin_0, LED11.anode
  N35: R24.Pin_0, LED10.anode
  N36: R28.Pin_0, LED9.anode
